# Fritzing sketch sin (saved by Fritzing 0.7.7b)
breadboards: 1

parts:
  U1 = Arduino Mega
  IC1 = IC, DIP package, 24 pins [chip_label=IC]
  IC2 = IC, DIP package, 4 pins [chip_label=IC part_number="Oscillator 8Mhz"]
  TRRS1 = Audio Jack (TRRS) 3.5mm [part_number="LUMBERG JEITA RC-5325A" package="RC-5325A [SMD]"]

nets:
  N1: U1.D13, IC1.pin18
  N2: U1.D12, IC1.pin17
  N3: U1.D11, IC1.pin16
  N4: U1.D10, IC1.pin15
  N5: U1.D9, IC1.pin9
  N6: U1.D8, IC1.pin8
  N7: U1.D7, IC1.pin7
  N8: U1.D6, IC1.pin6
  N9: U1.D5, IC1.pin5
  N10: U1.D4, IC1.pin4
  N11: U1.D3, IC1.pin3
  N12: U1.D2, IC1.pin2
  N13: U1.+5V, IC1.pin22, IC1.pin23, IC2.pin1
  N14: U1.GND, IC1.pin1, IC1.pin10, IC1.pin12, IC1.pin19, IC2.pin2, IC2.pin3
  N15: U1.A0, IC1.pin14
  N16: IC1.pin20, TRRS1.TIP
  N17: IC1.pin21, TRRS1.SLEEVE
  N18: IC1.pin24, IC2.pin4

notes:
  midi in
